# Fritzing sketch WaterCap (saved by Fritzing 0.9.3b)
breadboards: 1

parts:
  Part1 = Arduino Uno (Rev3)
  R1 = Resistor [tolerance=±5% resistance=220 package="0603 [SMD]"]

nets:
  N1: Part1.D3_PWM, R1.Pin_1
  N2: Part1.5V, R1.Pin_0

notes:
  Liquid flow meter
